// Logisim project Somador8bits.circ as structural Verilog: 1 circuit, main circuit main
module main (
  input  A7,
  input  B7,
  input  A4,
  input  B4,
  input  A6,
  input  B6,
  input  A5,
  input  B5,
  input  A3,
  input  B3,
  input  A2,
  input  B2,
  input  A1,
  input  B1,
  input  B0,
  input  A0,
  output S0,
  output Overflow,
  output S7,
  output S6,
  output S5,
  output S4,
  output S3,
  output S2,
  output S1
);

  wire and_1_out, and_2_out, and_3_out, and_4_out, and_5_out, and_6_out, and_7_out, and_8_out, and_9_out,
       and_10_out, and_11_out, and_12_out, and_13_out, and_14_out, and_15_out, and_16_out, and_17_out,
       and_18_out, and_19_out, and_20_out, and_21_out, and_22_out, or_2_out, or_3_out, or_4_out, or_5_out,
       or_6_out, or_7_out, xor_2_out, xor_4_out, xor_6_out, xor_8_out, xor_10_out, xor_12_out, xor_14_out;

  xor xor_1 (S7, xor_2_out, B7);
  or or_1 (Overflow, and_1_out, and_2_out, and_3_out);
  xor xor_2 (xor_2_out, A7, or_2_out);
  and and_1 (and_1_out, B7, or_2_out);
  and and_2 (and_2_out, A7, or_2_out);
  and and_3 (and_3_out, A7, B7);
  xor xor_3 (S6, xor_4_out, B6);
  or or_2 (or_2_out, and_4_out, and_5_out, and_6_out);
  xor xor_4 (xor_4_out, A6, or_3_out);
  and and_4 (and_4_out, B6, or_3_out);
  and and_5 (and_5_out, A6, or_3_out);
  and and_6 (and_6_out, A6, B6);
  xor xor_5 (S5, xor_6_out, B5);
  or or_3 (or_3_out, and_7_out, and_8_out, and_9_out);
  xor xor_6 (xor_6_out, A5, or_4_out);
  and and_7 (and_7_out, B5, or_4_out);
  and and_8 (and_8_out, A5, or_4_out);
  and and_9 (and_9_out, A5, B5);
  xor xor_7 (S4, xor_8_out, B4);
  or or_4 (or_4_out, and_10_out, and_11_out, and_12_out);
  xor xor_8 (xor_8_out, A4, or_5_out);
  and and_10 (and_10_out, B4, or_5_out);
  and and_11 (and_11_out, A4, or_5_out);
  and and_12 (and_12_out, A4, B4);
  xor xor_9 (S3, xor_10_out, B3);
  or or_5 (or_5_out, and_13_out, and_14_out, and_15_out);
  xor xor_10 (xor_10_out, A3, or_6_out);
  and and_13 (and_13_out, B3, or_6_out);
  and and_14 (and_14_out, A3, or_6_out);
  and and_15 (and_15_out, A3, B3);
  xor xor_11 (S2, xor_12_out, B2);
  or or_6 (or_6_out, and_16_out, and_17_out, and_18_out);
  xor xor_12 (xor_12_out, A2, or_7_out);
  and and_16 (and_16_out, B2, or_7_out);
  and and_17 (and_17_out, A2, or_7_out);
  and and_18 (and_18_out, A2, B2);
  or or_7 (or_7_out, and_19_out, and_20_out, and_21_out);
  xor xor_13 (S1, xor_14_out, B1);
  xor xor_14 (xor_14_out, A1, and_22_out);
  and and_19 (and_19_out, B1, and_22_out);
  and and_20 (and_20_out, A1, and_22_out);
  and and_21 (and_21_out, A1, B1);
  xor xor_15 (S0, A0, B0);
  and and_22 (and_22_out, B0, A0);
endmodule
