// Logisim project ULA16bits.circ as structural Verilog: 2 circuits, main circuit ula (1 bit)
module ula__1_bit (
  input  A,
  input  B,
  input  VEM_1,
  input  [2:0] C,
  input  ESQUERDA,
  input  DIREITA,
  output VAI_1,
  output out_8
);

  wire adder_1_cout, adder_1_out, and_1_out, and_2_out, nor_1_out, or_1_out, subtractor_1_bout,
       subtractor_1_out, xor_1_out;

  Adder #(.width(1)) adder_1 (.a(A), .b(B), .out(adder_1_out), .cin(VEM_1), .cout(adder_1_cout));
  Subtractor #(.width(1)) subtractor_1 (.a(A), .b(A), .out(subtractor_1_out), .bin(VEM_1), .bout(subtractor_1_bout));
  and and_1 (and_1_out, A, A);
  or or_1 (or_1_out, A, A);
  nor nor_1 (nor_1_out, A, B);
  xor xor_1 (xor_1_out, B, A);
  Multiplexer #(.enable("false")) multiplexer_1 (
    .in0(adder_1_cout), .in1(subtractor_1_bout), .out(VAI_1), .sel(and_2_out));
  and and_2 (and_2_out, ~C[2], ~C[1], C[0]);  // AND_Gate
  Multiplexer #(.select(3), .enable("false")) multiplexer_2 (
    .in0(adder_1_out), .in1(subtractor_1_out), .in2(and_1_out), .in3(or_1_out), .in4(nor_1_out),
    .in5(xor_1_out), .in6(ESQUERDA), .in7(DIREITA), .out(out_8), .sel(C));

  // Notes on the sheet:
  //   TABELA C
  //   000 - soma em C2
  //   010 - E bit a bit
  //   011 - OU bit a bit
  //   100 - NOU bit a bit
  //   101 - XOU bit a bit
  //   001 - subtração em C2
  //   110 - deslocamento p/ esquerda
  //   111 - deslocamento p/ direita
endmodule

module ula__16_bits (
  input  [15:0] B,
  input  [15:0] A,
  input  [2:0] C,
  output OVERFLOW,
  output [15:0] S
);

  wire ula_1_bit_2_vai_1, ula_1_bit_3_vai_1, ula_1_bit_4_vai_1, ula_1_bit_5_vai_1, ula_1_bit_6_vai_1,
       ula_1_bit_7_vai_1, ula_1_bit_8_vai_1, ula_1_bit_9_vai_1, ula_1_bit_10_vai_1, ula_1_bit_11_vai_1,
       ula_1_bit_12_vai_1, ula_1_bit_13_vai_1, ula_1_bit_14_vai_1, ula_1_bit_15_vai_1, ula_1_bit_16_vai_1;

  ula__1_bit ula_1_bit_1 (
    .ESQUERDA(A[14]), .VAI_1(OVERFLOW), .out_8(S[15]), .DIREITA(1'b0), .A(A[15]), .B(B[15]),
    .VEM_1(ula_1_bit_2_vai_1), .C(C));
  ula__1_bit ula_1_bit_2 (
    .ESQUERDA(A[13]), .VAI_1(ula_1_bit_2_vai_1), .out_8(S[14]), .DIREITA(A[15]), .A(A[14]), .B(B[14]),
    .VEM_1(ula_1_bit_3_vai_1), .C(C));
  ula__1_bit ula_1_bit_3 (
    .ESQUERDA(A[12]), .VAI_1(ula_1_bit_3_vai_1), .out_8(S[13]), .DIREITA(A[14]), .A(A[13]), .B(B[13]),
    .VEM_1(ula_1_bit_4_vai_1), .C(C));
  ula__1_bit ula_1_bit_4 (
    .ESQUERDA(A[11]), .VAI_1(ula_1_bit_4_vai_1), .out_8(S[12]), .DIREITA(A[13]), .A(A[12]), .B(B[12]),
    .VEM_1(ula_1_bit_5_vai_1), .C(C));
  ula__1_bit ula_1_bit_5 (
    .ESQUERDA(A[10]), .VAI_1(ula_1_bit_5_vai_1), .out_8(S[11]), .DIREITA(A[12]), .A(A[11]), .B(B[11]),
    .VEM_1(ula_1_bit_6_vai_1), .C(C));
  ula__1_bit ula_1_bit_6 (
    .ESQUERDA(A[9]), .VAI_1(ula_1_bit_6_vai_1), .out_8(S[10]), .DIREITA(A[11]), .A(A[10]), .B(B[10]),
    .VEM_1(ula_1_bit_7_vai_1), .C(C));
  ula__1_bit ula_1_bit_7 (
    .ESQUERDA(A[8]), .VAI_1(ula_1_bit_7_vai_1), .out_8(S[9]), .DIREITA(A[10]), .A(A[9]), .B(B[9]),
    .VEM_1(ula_1_bit_8_vai_1), .C(C));
  ula__1_bit ula_1_bit_8 (
    .ESQUERDA(A[7]), .VAI_1(ula_1_bit_8_vai_1), .out_8(S[8]), .DIREITA(A[9]), .A(A[8]), .B(B[8]),
    .VEM_1(ula_1_bit_9_vai_1), .C(C));
  ula__1_bit ula_1_bit_9 (
    .ESQUERDA(A[6]), .VAI_1(ula_1_bit_9_vai_1), .out_8(S[7]), .DIREITA(A[8]), .A(A[7]), .B(B[7]),
    .VEM_1(ula_1_bit_10_vai_1), .C(C));
  ula__1_bit ula_1_bit_10 (
    .ESQUERDA(A[5]), .VAI_1(ula_1_bit_10_vai_1), .out_8(S[6]), .DIREITA(A[7]), .A(A[6]), .B(B[6]),
    .VEM_1(ula_1_bit_11_vai_1), .C(C));
  ula__1_bit ula_1_bit_11 (
    .ESQUERDA(A[4]), .VAI_1(ula_1_bit_11_vai_1), .out_8(S[5]), .DIREITA(A[6]), .A(A[5]), .B(B[5]),
    .VEM_1(ula_1_bit_12_vai_1), .C(C));
  ula__1_bit ula_1_bit_12 (
    .ESQUERDA(A[3]), .VAI_1(ula_1_bit_12_vai_1), .out_8(S[4]), .DIREITA(A[5]), .A(A[4]), .B(B[4]),
    .VEM_1(ula_1_bit_13_vai_1), .C(C));
  ula__1_bit ula_1_bit_13 (
    .ESQUERDA(A[2]), .VAI_1(ula_1_bit_13_vai_1), .out_8(S[3]), .DIREITA(A[4]), .A(A[3]), .B(B[3]),
    .VEM_1(ula_1_bit_14_vai_1), .C(C));
  ula__1_bit ula_1_bit_14 (
    .ESQUERDA(A[1]), .VAI_1(ula_1_bit_14_vai_1), .out_8(S[2]), .DIREITA(A[3]), .A(A[2]), .B(B[2]),
    .VEM_1(ula_1_bit_15_vai_1), .C(C));
  ula__1_bit ula_1_bit_15 (
    .ESQUERDA(A[0]), .VAI_1(ula_1_bit_15_vai_1), .out_8(S[1]), .DIREITA(A[2]), .A(A[1]), .B(B[1]),
    .VEM_1(ula_1_bit_16_vai_1), .C(C));
  ula__1_bit ula_1_bit_16 (
    .ESQUERDA(1'b0), .VAI_1(ula_1_bit_16_vai_1), .out_8(S[0]), .DIREITA(A[1]), .A(A[0]), .B(B[0]),
    .VEM_1(1'b0), .C(C));
endmodule
